# Fritzing sketch schem (saved by Fritzing 1.0.2b)

parts:
  8x8_LED_Modul_mit_MAX1 = 8x8 LED Modul mit MAX7219 [package=THT]
  8x8_LED_Modul_mit_MAX2 = 8x8 LED Modul mit MAX7219 [package=THT]
  Componente1 = Arduino Mega 2560 (Rev3)
  J1 = Basic Servo
  J2 = Basic Servo

nets:
  N1: 8x8_LED_Modul_mit_MAX1.DIN_Eingang, Componente1.D12_PWM
  N2: 8x8_LED_Modul_mit_MAX1.CS_Eingang, Componente1.D10_PWM
  N3: 8x8_LED_Modul_mit_MAX1.CLK_Eingang, Componente1.D11_PWM
  N4: 8x8_LED_Modul_mit_MAX2.DIN_Eingang, Componente1.D7_PWM
  N5: 8x8_LED_Modul_mit_MAX2.CS_Eingang, Componente1.D8_PWM
  N6: 8x8_LED_Modul_mit_MAX2.CLK_Eingang, Componente1.D9_PWM
  5V: Componente1.5V, J2.vcc
  N7: Componente1.D5_PWM, J2.pulse
  N8: Componente1.D6_PWM, J1.pulse
